// Logisim project ALU1.circ as structural Verilog
module add_circuit (
  input  [31:0] a,
  input  [31:0] b,
  input  [3:0] aluop,
  input  output_inverted,
  input  output_inc,
  input  clk,
  input  rst,
  output [31:0] res_low,
  output [31:0] res_high
);

  wire adder_1_cout;

  Adder #(.width(32)) adder_1 (.a(a), .b(b), .out(res_low), .cin(1'b0), .cout(adder_1_cout));
  assign res_high = {{31{1'b0}}, adder_1_cout};  // Bit_Extender bit_extender_1
endmodule

module sub_circuit (
  input  [31:0] a,
  input  [31:0] b,
  input  [3:0] aluop,
  input  output_inverted,
  input  output_inc,
  input  clk,
  input  rst,
  output [31:0] res_low,
  output [31:0] res_high
);

  wire subtractor_1_bout;
  wire [31:0] bit_extender_1_out, subtractor_1_out;

  Subtractor #(.width(32)) subtractor_1 (.a(a), .b(b), .out(subtractor_1_out), .bin(1'b0), .bout(subtractor_1_bout));
  assign bit_extender_1_out = {{31{1'b0}}, subtractor_1_bout};  // Bit_Extender bit_extender_1
endmodule
