// Logisim project ALU3.circ as structural Verilog
module main (
  input  in_1,
  input  in_2
);
endmodule

module xor_circuit (
  input  [31:0] a,
  input  [31:0] b,
  output [31:0] res_low
);

  assign res_low = a ^ b;  // XOR_Gate xor_1, 32 bits wide
endmodule

module or_circuit (
  input  [31:0] a,
  input  [31:0] b,
  output [31:0] res_low
);

  assign res_low = a | b;  // OR_Gate or_1, 32 bits wide
endmodule

module and_circuit (
  input  [31:0] a,
  input  [31:0] b,
  output [31:0] res_low
);

  assign res_low = a & b;  // AND_Gate and_1, 32 bits wide
endmodule

module add_circuit (
  input  [31:0] a,
  input  [31:0] b,
  input  [3:0] aluop,
  input  output_inverted,
  input  output_inc,
  input  clk,
  input  rst,
  output [31:0] res_low,
  output [31:0] res_high
);

  wire adder_1_cout;

  Adder #(.width(32)) adder_1 (.a(a), .b(b), .out(res_low), .cin(1'b0), .cout(adder_1_cout));
  assign res_high = {{31{1'b0}}, adder_1_cout};  // Bit_Extender bit_extender_1
endmodule

module sub_circuit (
  input  [31:0] a,
  input  [31:0] b,
  input  [3:0] aluop,
  input  output_inverted,
  input  output_inc,
  input  clk,
  input  rst,
  output [31:0] res_low,
  output [31:0] res_high
);

  wire subtractor_1_bout;

  Subtractor #(.width(32)) subtractor_1 (.a(a), .b(b), .out(res_low), .bin(1'b0), .bout(subtractor_1_bout));
  assign res_high = {{31{1'b0}}, subtractor_1_bout};  // Bit_Extender bit_extender_1
endmodule

module sll_circuit (
  input  [31:0] a,
  input  [4:0] num_shift,
  output [63:0] result
);

  wire [63:0] extended, multiplexer_1_out, multiplexer_2_out, multiplexer_3_out, multiplexer_4_out;
  wire [63:2] s2;
  wire [63:4] s3;
  wire [63:8] s4;
  wire [63:16] s5;

  assign extended = {{32{1'b0}}, a};  // Bit_Extender bit_extender_1
  Multiplexer #(.width(64)) multiplexer_1 (
    .in0(extended), .in1({extended[62:0], 1'b0}), .out(multiplexer_1_out), .sel(num_shift[0]));
  Multiplexer #(.width(64)) multiplexer_2 (
    .in0(multiplexer_1_out), .in1({s2, 2'b00}), .out(multiplexer_2_out), .sel(num_shift[1]));
  Multiplexer #(.width(64)) multiplexer_3 (
    .in0(multiplexer_2_out), .in1({s3, 4'b0000}), .out(multiplexer_3_out), .sel(num_shift[2]));
  Multiplexer #(.width(64)) multiplexer_4 (
    .in0(multiplexer_3_out), .in1({s4, {8{1'b0}}}), .out(multiplexer_4_out), .sel(num_shift[3]));
  Multiplexer #(.width(64)) multiplexer_5 (
    .in0(multiplexer_4_out), .in1({s5, {16{1'b0}}}), .out(result), .sel(num_shift[4]));

  // Other names for the same wires on the sheet: s1[63:1] = extended[62:0]; bit0 = num_shift[0]; bit1 = num_shift[1];
  //   bit2 = num_shift[2]; bit3 = num_shift[3]; bit4 = num_shift[4]; stage_1[61:0] = s2; stage_2[59:0] = s3;
  //   stage_3[55:0] = s4; stage_4[47:0] = s5
endmodule

module srl_circuit (
  input  [31:0] a,
  input  [4:0] num_shift,
  output [63:0] result
);

  wire [47:0] s5;
  wire [55:0] s4;
  wire [59:0] s3;
  wire [61:0] s2;
  wire [63:0] extended, multiplexer_1_out, multiplexer_2_out, multiplexer_3_out, multiplexer_4_out;

  assign extended = {{32{1'b0}}, a};  // Bit_Extender bit_extender_1
  Multiplexer #(.width(64)) multiplexer_1 (
    .in0(extended), .in1({1'b0, extended[63:1]}), .out(multiplexer_1_out), .sel(num_shift[0]));
  Multiplexer #(.width(64)) multiplexer_2 (
    .in0(multiplexer_1_out), .in1({2'b00, s2}), .out(multiplexer_2_out), .sel(num_shift[1]));
  Multiplexer #(.width(64)) multiplexer_3 (
    .in0(multiplexer_2_out), .in1({4'b0000, s3}), .out(multiplexer_3_out), .sel(num_shift[2]));
  Multiplexer #(.width(64)) multiplexer_4 (
    .in0(multiplexer_3_out), .in1({{8{1'b0}}, s4}), .out(multiplexer_4_out), .sel(num_shift[3]));
  Multiplexer #(.width(64)) multiplexer_5 (
    .in0(multiplexer_4_out), .in1({{16{1'b0}}, s5}), .out(result), .sel(num_shift[4]));

  // Other names for the same wires on the sheet: bit0 = num_shift[0]; bit1 = num_shift[1]; bit2 = num_shift[2];
  //   bit3 = num_shift[3]; bit4 = num_shift[4]; s1[62:0] = extended[63:1]; stage_1[63:2] = s2; stage_2[63:4] = s3;
  //   stage_3[63:8] = s4; stage_4[63:16] = s5
endmodule

module sra_circuit (
  input  [31:0] a,
  input  [4:0] num_shift,
  output [63:0] result
);

  wire [63:0] extended, multiplexer_1_out, multiplexer_2_out, multiplexer_3_out, multiplexer_4_out, s2, s3,
       s4, s5;

  assign extended = {{32{1'b0}}, a};  // Bit_Extender bit_extender_1
  Multiplexer #(.width(64)) multiplexer_1 (
    .in0(extended), .in1({{2{extended[63]}}, extended[62:1]}), .out(multiplexer_1_out), .sel(num_shift[0]));
  Multiplexer #(.width(64)) multiplexer_2 (
    .in0(multiplexer_1_out), .in1({s2[63:62], s2[63:62], s2[59:0]}), .out(multiplexer_2_out),
    .sel(num_shift[1]));
  Multiplexer #(.width(64)) multiplexer_3 (
    .in0(multiplexer_2_out), .in1({s3[63:60], s3[63:60], s3[55:0]}), .out(multiplexer_3_out),
    .sel(num_shift[2]));
  Multiplexer #(.width(64)) multiplexer_4 (
    .in0(multiplexer_3_out), .in1({s4[63:56], s4[63:56], s4[47:0]}), .out(multiplexer_4_out),
    .sel(num_shift[3]));
  Multiplexer #(.width(64)) multiplexer_5 (
    .in0(multiplexer_4_out), .in1({s5[63:48], s5[63:48], s5[31:0]}), .out(result), .sel(num_shift[4]));

  // Other names for the same wires on the sheet: bit0 = num_shift[0]; bit1 = num_shift[1]; bit2 = num_shift[2];
  //   bit3 = num_shift[3]; bit4 = num_shift[4]; s1[63:0] = {{2{extended[63]}}, extended[62:1]};
  //   stage_1[63:2] = {s2[63:62], s2[59:0]}; s2[61:60] = s2[63:62]; stage_2[63:4] = {s3[63:60], s3[55:0]};
  //   s3[59:56] = s3[63:60]; stage_3[63:8] = {s4[63:56], s4[47:0]}; s4[55:48] = s4[63:56];
  //   stage_4[63:16] = {s5[63:48], s5[31:0]}; s5[47:32] = s5[63:48]
endmodule

module rotr_circuit (
  input  [31:0] a,
  input  [4:0] num_shift,
  output [63:0] result
);

  wire [31:0] multiplexer_1_out, multiplexer_2_out, multiplexer_3_out, multiplexer_4_out;
  wire [63:0] s1, s2, s3, s4, s5;
  wire [63:32] extended;

  Multiplexer #(.width(32)) multiplexer_1 (.in0(a), .in1(s1[31:0]), .out(multiplexer_1_out), .sel(num_shift[0]));
  Multiplexer #(.width(32)) multiplexer_2 (
    .in0(multiplexer_1_out), .in1(s2[31:0]), .out(multiplexer_2_out), .sel(num_shift[1]));
  Multiplexer #(.width(32)) multiplexer_3 (
    .in0(multiplexer_2_out), .in1(s3[31:0]), .out(multiplexer_3_out), .sel(num_shift[2]));
  Multiplexer #(.width(32)) multiplexer_4 (
    .in0(multiplexer_3_out), .in1(s4[31:0]), .out(multiplexer_4_out), .sel(num_shift[3]));
  Multiplexer #(.width(32)) multiplexer_5 (
    .in0(multiplexer_4_out), .in1(s5[31:0]), .out(result[31:0]), .sel(num_shift[4]));
  // Pins of 32 and 64 bits meet at s3
  // Pins of 32 and 64 bits meet at s2
  // Pins of 32 and 64 bits meet at s4
  // Pins of 32 and 64 bits meet at {extended, a}
  // Pins of 32 and 64 bits meet at s5
  // Pins of 32 and 64 bits meet at result
  // Pins of 32 and 64 bits meet at s1

  // Other names for the same wires on the sheet: extended[31:0] = a; bit0 = num_shift[0]; bit1 = num_shift[1];
  //   bit2 = num_shift[2]; bit3 = num_shift[3]; bit4 = num_shift[4]; stage_1[63:0] = {s2[61:0], s2[63:62]};
  //   stage_2[63:0] = {s3[59:0], s3[63:60]}; stage_3[63:0] = {s4[55:0], s4[63:56]};
  //   stage_4[63:0] = {s5[47:0], s5[63:48]}
endmodule
