// Logisim project ALU4.circ as structural Verilog
module xor_circuit (
  input  [31:0] a,
  input  [31:0] b,
  output [31:0] res_low
);

  assign res_low = a ^ b;  // XOR_Gate xor_1, 32 bits wide
endmodule

module or_circuit (
  input  [31:0] a,
  input  [31:0] b,
  output [31:0] res_low
);

  assign res_low = a | b;  // OR_Gate or_1, 32 bits wide
endmodule

module and_circuit (
  input  [31:0] a,
  input  [31:0] b,
  output [31:0] res_low
);

  assign res_low = a & b;  // AND_Gate and_1, 32 bits wide
endmodule

module add_circuit (
  input  [31:0] a,
  input  [31:0] b,
  input  [3:0] aluop,
  input  output_inverted,
  input  output_inc,
  input  clk,
  input  rst,
  output [31:0] res_low,
  output [31:0] res_high
);

  wire adder_1_cout;

  Adder #(.width(32)) adder_1 (.a(a), .b(b), .out(res_low), .cin(1'b0), .cout(adder_1_cout));
  assign res_high = {{31{1'b0}}, adder_1_cout};  // Bit_Extender bit_extender_1
endmodule

module sub_circuit (
  input  [31:0] a,
  input  [31:0] b,
  input  [3:0] aluop,
  input  output_inverted,
  input  output_inc,
  input  clk,
  input  rst,
  output [31:0] res_low,
  output [31:0] res_high
);

  wire subtractor_1_bout;

  Subtractor #(.width(32)) subtractor_1 (.a(a), .b(b), .out(res_low), .bin(1'b0), .bout(subtractor_1_bout));
  assign res_high = {{31{1'b0}}, subtractor_1_bout};  // Bit_Extender bit_extender_1
endmodule

module sll_circuit (
);

  wire bit0, bit1, bit2, bit3, bit4;
  wire [31:0] a;
  wire [63:0] extended, multiplexer_1_out, multiplexer_2_out, multiplexer_3_out, multiplexer_4_out, stage_5;
  wire [63:2] s2;
  wire [63:4] s3;
  wire [63:8] s4;
  wire [63:16] s5;

  assign extended = {{32{1'b0}}, a};  // Bit_Extender bit_extender_1
  Multiplexer #(.width(64)) multiplexer_1 (
    .in0(extended), .in1({extended[62:0], 1'b0}), .out(multiplexer_1_out), .sel(bit0));
  Multiplexer #(.width(64)) multiplexer_2 (
    .in0(multiplexer_1_out), .in1({s2, 2'b00}), .out(multiplexer_2_out), .sel(bit1));
  Multiplexer #(.width(64)) multiplexer_3 (
    .in0(multiplexer_2_out), .in1({s3, 4'b0000}), .out(multiplexer_3_out), .sel(bit2));
  Multiplexer #(.width(64)) multiplexer_4 (
    .in0(multiplexer_3_out), .in1({s4, {8{1'b0}}}), .out(multiplexer_4_out), .sel(bit3));
  Multiplexer #(.width(64)) multiplexer_5 (.in0(multiplexer_4_out), .in1({s5, {16{1'b0}}}), .out(stage_5), .sel(bit4));

  // Other names for the same wires on the sheet: s1[63:1] = extended[62:0];
  //   num_shift[4:0] = {bit4, bit3, bit2, bit1, bit0}; stage_1[61:0] = s2; stage_2[59:0] = s3; stage_3[55:0] = s4;
  //   stage_4[47:0] = s5
endmodule

module srl_circuit (
);

  wire bit0, bit1, bit2, bit3, bit4;
  wire [31:0] a;
  wire [47:0] s5;
  wire [55:0] s4;
  wire [59:0] s3;
  wire [61:0] s2;
  wire [63:0] extended, multiplexer_1_out, multiplexer_2_out, multiplexer_3_out, multiplexer_4_out, stage_5;

  assign extended = {{32{1'b0}}, a};  // Bit_Extender bit_extender_1
  Multiplexer #(.width(64)) multiplexer_1 (
    .in0(extended), .in1({1'b0, extended[63:1]}), .out(multiplexer_1_out), .sel(bit0));
  Multiplexer #(.width(64)) multiplexer_2 (
    .in0(multiplexer_1_out), .in1({2'b00, s2}), .out(multiplexer_2_out), .sel(bit1));
  Multiplexer #(.width(64)) multiplexer_3 (
    .in0(multiplexer_2_out), .in1({4'b0000, s3}), .out(multiplexer_3_out), .sel(bit2));
  Multiplexer #(.width(64)) multiplexer_4 (
    .in0(multiplexer_3_out), .in1({{8{1'b0}}, s4}), .out(multiplexer_4_out), .sel(bit3));
  Multiplexer #(.width(64)) multiplexer_5 (.in0(multiplexer_4_out), .in1({{16{1'b0}}, s5}), .out(stage_5), .sel(bit4));

  // Other names for the same wires on the sheet: num_shift[4:0] = {bit4, bit3, bit2, bit1, bit0};
  //   s1[62:0] = extended[63:1]; stage_1[63:2] = s2; stage_2[63:4] = s3; stage_3[63:8] = s4; stage_4[63:16] = s5
endmodule

module Carry_Select_Adder (
  input  c_in,
  input  [31:0] a,
  input  [31:0] b,
  output [63:0] res
);

  wire adder_1_cout, adder_2_cout, adder_3_cout, adder_4_cout, adder_5_cout, adder_6_cout, adder_7_cout,
       adder_8_cout, adder_9_cout, adder_10_cout, adder_11_cout, adder_12_cout, adder_13_cout, adder_14_cout,
       adder_15_cout, multiplexer_1_out, multiplexer_2_out, multiplexer_3_out, multiplexer_4_out,
       multiplexer_5_out, multiplexer_6_out;
  wire [3:0] adder_1_out, adder_2_out, adder_3_out, adder_4_out, adder_5_out, adder_6_out, adder_7_out,
       adder_9_out, adder_10_out, adder_11_out, adder_12_out, adder_13_out, adder_14_out, adder_15_out;

  Adder #(.width(4)) adder_1 (.a(a[7:4]), .b(b[7:4]), .out(adder_1_out), .cout(adder_1_cout));  // open: cin
  Adder #(.width(4)) adder_2 (.a(a[11:8]), .b(b[11:8]), .out(adder_2_out), .cout(adder_2_cout));  // open: cin
  Adder #(.width(4)) adder_3 (.a(a[15:12]), .b(b[15:12]), .out(adder_3_out), .cout(adder_3_cout));  // open: cin
  Adder #(.width(4)) adder_4 (.a(a[19:16]), .b(b[19:16]), .out(adder_4_out), .cout(adder_4_cout));  // open: cin
  Adder #(.width(4)) adder_5 (.a(a[23:20]), .b(b[23:20]), .out(adder_5_out), .cout(adder_5_cout));  // open: cin
  Adder #(.width(4)) adder_6 (.a(a[27:24]), .b(b[27:24]), .out(adder_6_out), .cout(adder_6_cout));  // open: cin
  Adder #(.width(4)) adder_7 (.a(a[31:28]), .b(b[31:28]), .out(adder_7_out), .cout(adder_7_cout));  // open: cin
  Adder #(.width(4)) adder_8 (.a(a[3:0]), .b(b[3:0]), .out(res[3:0]), .cin(c_in), .cout(adder_8_cout));
  Adder #(.width(4)) adder_9 (.a(a[7:4]), .b(b[7:4]), .out(adder_9_out), .cin(1'b1), .cout(adder_9_cout));
  Adder #(.width(4)) adder_10 (.a(a[11:8]), .b(b[11:8]), .out(adder_10_out), .cin(1'b1), .cout(adder_10_cout));
  Adder #(.width(4)) adder_11 (.a(a[15:12]), .b(b[15:12]), .out(adder_11_out), .cin(1'b1), .cout(adder_11_cout));
  Adder #(.width(4)) adder_12 (.a(a[19:16]), .b(b[19:16]), .out(adder_12_out), .cin(1'b1), .cout(adder_12_cout));
  Adder #(.width(4)) adder_13 (.a(a[23:20]), .b(b[23:20]), .out(adder_13_out), .cin(1'b1), .cout(adder_13_cout));
  Adder #(.width(4)) adder_14 (.a(a[27:24]), .b(b[27:24]), .out(adder_14_out), .cin(1'b1), .cout(adder_14_cout));
  Adder #(.width(4)) adder_15 (.a(a[31:28]), .b(b[31:28]), .out(adder_15_out), .cin(1'b1), .cout(adder_15_cout));
  Multiplexer multiplexer_1 (.in0(adder_1_cout), .in1(adder_9_cout), .out(multiplexer_1_out), .sel(adder_8_cout));
  Multiplexer multiplexer_2 (.in0(adder_2_cout), .in1(adder_10_cout), .out(multiplexer_2_out), .sel(multiplexer_1_out));
  Multiplexer multiplexer_3 (.in0(adder_3_cout), .in1(adder_11_cout), .out(multiplexer_3_out), .sel(multiplexer_2_out));
  Multiplexer multiplexer_4 (.in0(adder_4_cout), .in1(adder_12_cout), .out(multiplexer_4_out), .sel(multiplexer_3_out));
  Multiplexer multiplexer_5 (.in0(adder_5_cout), .in1(adder_13_cout), .out(multiplexer_5_out), .sel(multiplexer_4_out));
  Multiplexer multiplexer_6 (.in0(adder_6_cout), .in1(adder_14_cout), .out(multiplexer_6_out), .sel(multiplexer_5_out));
  Multiplexer multiplexer_7 (.in0(adder_7_cout), .in1(adder_15_cout), .out(res[32]), .sel(multiplexer_6_out));
  Multiplexer #(.width(4)) multiplexer_8 (.in0(adder_1_out), .in1(adder_9_out), .out(res[7:4]), .sel(adder_8_cout));
  Multiplexer #(.width(4)) multiplexer_9 (
    .in0(adder_2_out), .in1(adder_10_out), .out(res[11:8]), .sel(multiplexer_1_out));
  Multiplexer #(.width(4)) multiplexer_10 (
    .in0(adder_3_out), .in1(adder_11_out), .out(res[15:12]), .sel(multiplexer_2_out));
  Multiplexer #(.width(4)) multiplexer_11 (
    .in0(adder_4_out), .in1(adder_12_out), .out(res[19:16]), .sel(multiplexer_3_out));
  Multiplexer #(.width(4)) multiplexer_12 (
    .in0(adder_5_out), .in1(adder_13_out), .out(res[23:20]), .sel(multiplexer_4_out));
  Multiplexer #(.width(4)) multiplexer_13 (
    .in0(adder_6_out), .in1(adder_14_out), .out(res[27:24]), .sel(multiplexer_5_out));
  Multiplexer #(.width(4)) multiplexer_14 (
    .in0(adder_7_out), .in1(adder_15_out), .out(res[31:28]), .sel(multiplexer_6_out));

  assign res[63:33] = {31{1'b0}};
endmodule

module Shift_Logical_Left_circuit (
  input  [4:0] shamt,
  input  [31:0] A,
  output [63:0] O,
  output [63:0] res
);

  wire [63:0] extended_64;
  wire [63:1] shift_1;
  wire [63:2] shift_2;
  wire [63:4] shift_4;
  wire [63:7] shift_8;
  wire [63:16] shift_16;
  wire [63:48] stage_8;
  wire [63:57] stage_4;
  wire [63:60] stage_2;
  wire [63:62] stage_1;

  Multiplexer #(.width(64)) multiplexer_1 (
    .in0({stage_8, shift_16}), .in1({shift_16, {16{1'b0}}}), .out(res), .sel(shamt[4]));
  Multiplexer #(.width(64)) multiplexer_2 (
    .in0({stage_1, shift_2}), .in1({shift_2, 2'b00}), .out({stage_2, shift_4}), .sel(shamt[1]));
  Multiplexer #(.width(64)) multiplexer_3 (
    .in0({stage_2, shift_4}), .in1({shift_4, 4'b0000}), .out({stage_4, shift_8}), .sel(shamt[2]));
  Multiplexer #(.width(64)) multiplexer_4 (
    .in0(extended_64), .in1({shift_1, 1'b0}), .out({stage_1, shift_2}), .sel(shamt[0]));
  Multiplexer #(.width(64)) multiplexer_5 (
    .in0({stage_4, shift_8}), .in1({shift_8, {7{1'b0}}}), .out({stage_8, shift_16}), .sel(shamt[3]));

  assign O = {{32{1'b0}}, A};

  // Other names for the same wires on the sheet: b0 = shamt[0]; b1 = shamt[1]; b2 = shamt[2]; b3 = shamt[3];
  //   b4 = shamt[4]; stage_2[59:0] = shift_4; stage_8[47:0] = shift_16; stage_1[61:0] = shift_2;
  //   stage_4[56:0] = shift_8; stage_16[63:0] = res
endmodule

module CSA (
  input  [31:0] a,
  input  [31:0] b,
  input  [31:0] c,
  input  c_in,
  output [63:0] res
);

  wire [31:0] and_1_out, and_2_out, and_3_out, carry_out, sum_out;
  wire [63:0] shift_logical_left_circuit_1_res;

  ExactlyOne sum[31:0] (.out(sum_out), .in0(a), .in1(b), .in2(c));
  assign and_1_out = a & b;  // AND_Gate and_1, 32 bits wide
  assign and_2_out = b & c;  // AND_Gate and_2, 32 bits wide
  assign carry_out = and_1_out | and_2_out | and_3_out;  // OR_Gate carry, 32 bits wide
  assign and_3_out = a & c;  // AND_Gate and_3, 32 bits wide
  Shift_Logical_Left_circuit shift_logical_left_circuit_1 (
    .shamt(5'b00001), .A(carry_out), .res(shift_logical_left_circuit_1_res));  // open: O
  Carry_Select_Adder carry_select_adder_1 (
    .c_in(c_in), .a(sum_out), .b(shift_logical_left_circuit_1_res[31:0]), .res(res));
endmodule
