// Logisim project ALU5.circ as structural Verilog: 18 circuits, main circuit main
module main (
  input  [31:0] b,
  input  [31:0] a,
  input  output_inc,
  input  output_inverted,
  input  [3:0] aluop,
  input  clk,
  input  rst,
  output [31:0] res_low,
  output [31:0] res_high,
  output done
);

  wire and_1_out, comparator_1_eq, comparator_2_eq, comparator_3_eq, div_done, mul_done, not_1_out,
       not_2_out, or_1_out;
  wire [5:0] clo_circuit_1_res, clz_circuit_1_out_2;
  wire [31:0] add_circ_1_res_high, add_circ_1_res_low, add_circ_2_res_low, and_circuit_1_res_low,
       bit_extender_7_out, or_circuit_1_res_low, register_1_q, register_2_q, rotr_circuit_1_result,
       xor_circuit_1_res_low;
  wire [63:0] addr, andr, clor, clzr, divr, mulr, multiplexer_1_out, multiplexer_2_out, not_3_out, orr,
       rotrr, sllr, srar, srlr, subr, xorr;

  xor_circuit xor_circuit_1 (.a(a), .b(b), .res_low(xor_circuit_1_res_low));
  or_circuit or_circuit_1 (.a(a), .b(b), .res_low(or_circuit_1_res_low));
  and_circuit and_circuit_1 (.a(a), .b(b), .res_low(and_circuit_1_res_low));
  add_circuit add_circuit_1 (.c_in(1'b0), .a(a), .b(b), .res(addr));
  sub_circuit sub_circuit_1 (.a(a), .b(b), .res(subr));
  clo_circuit clo_circuit_1 (.A(a), .res(clo_circuit_1_res));
  clz_circuit clz_circuit_1 (.A(a), .out_2(clz_circuit_1_out_2));
  assign xorr = {{32{1'b0}}, xor_circuit_1_res_low};  // Bit_Extender bit_extender_1
  assign orr = {{32{1'b0}}, or_circuit_1_res_low};  // Bit_Extender bit_extender_2
  assign andr = {{32{1'b0}}, and_circuit_1_res_low};  // Bit_Extender bit_extender_3
  assign clor = {{58{1'b0}}, clo_circuit_1_res};  // Bit_Extender bit_extender_4
  assign clzr = {{58{1'b0}}, clz_circuit_1_out_2};  // Bit_Extender bit_extender_5
  Comparator #(.mode("unsigned"), .width(4)) comparator_1 (
    .a(aluop), .b(4'b0011), .eq(comparator_1_eq));  // open: gt, lt
  sll_circuit sll_circuit_1 (.a(a), .num_shift(b[4:0]), .result(sllr));
  srl_circuit srl_circuit_1 (.a(a), .num_shift(b[4:0]), .result(srlr));
  sra_circuit sra_circuit_1 (.a(a), .num_shift(b[4:0]), .result(srar));
  rotr_circuit rotr_circuit_1 (.a(a), .num_shift(b[4:0]), .result(rotr_circuit_1_result));
  Register #(.width(32)) register_1 (.D(a), .clk(clk), .Q(register_1_q));  // open: en, clr
  Register #(.width(32)) register_2 (.D(b), .clk(clk), .Q(register_2_q));  // open: en, clr
  assign rotrr = {{32{1'b0}}, rotr_circuit_1_result};  // Bit_Extender bit_extender_6
  div_circuit div_circuit_1 (
    .divisor(b), .dividend(a), .start(and_1_out), .clk(clk), .quotient(divr[31:0]), .remainder(divr[63:32]),
    .done(div_done));
  not not_1 (not_1_out, comparator_2_eq);
  Comparator #(.mode("unsigned"), .width(32)) comparator_2 (
    .a(register_1_q), .b(a), .eq(comparator_2_eq));  // open: gt, lt
  not not_2 (not_2_out, comparator_3_eq);
  Comparator #(.mode("unsigned"), .width(32)) comparator_3 (
    .a(register_2_q), .b(b), .eq(comparator_3_eq));  // open: gt, lt
  or or_1 (or_1_out, not_1_out, not_2_out);
  and and_1 (and_1_out, or_1_out, comparator_1_eq);
  Multiplexer #(.select(4), .width(64)) multiplexer_1 (
    .in0(addr), .in1(subr), .in2(mulr), .in3(divr), .in4(andr), .in5(orr), .in6(xorr), .in7(clor),
    .in8(clzr), .in9(sllr), .in10(srlr), .in11(srar), .in12(rotrr), .out(multiplexer_1_out), .sel(aluop));  // open: in13, in14, in15
  assign not_3_out = ~multiplexer_1_out;  // NOT_Gate not_3, 64 bits wide
  Multiplexer #(.width(64)) multiplexer_2 (
    .in0(multiplexer_1_out), .in1(not_3_out), .out(multiplexer_2_out), .sel(output_inverted));
  Multiplexer #(.select(4)) multiplexer_3 (
    .in0(1'b1), .in1(1'b1), .in2(div_done), .in3(mul_done), .in4(1'b1), .in5(1'b1), .in6(1'b1), .in7(1'b1),
    .in8(1'b1), .in9(1'b1), .in10(1'b1), .in11(1'b1), .in12(1'b1), .out(done), .sel(aluop));  // open: in13, in14, in15
  assign bit_extender_7_out = {{31{1'b0}}, output_inc};  // Bit_Extender bit_extender_7
  add_circ add_circ_1 (
    .a(multiplexer_2_out[31:0]), .b(bit_extender_7_out), .res_low(add_circ_1_res_low),
    .res_high(add_circ_1_res_high));
  add_circ add_circ_2 (
    .a(multiplexer_2_out[63:32]), .b(add_circ_1_res_high), .res_low(add_circ_2_res_low));  // open: res_high
  Register #(.width(32)) register_3 (.D(add_circ_1_res_low), .en(1'b1), .clk(clk), .Q(res_low), .clr(rst));
  Register #(.width(32)) register_4 (.D(add_circ_2_res_low), .en(1'b1), .clk(clk), .Q(res_high), .clr(rst));

  // Other names for the same wires on the sheet: aluop_tunnel[3:0] = aluop
endmodule

module xor_circuit (
  input  [31:0] a,
  input  [31:0] b,
  output [31:0] res_low
);

  assign res_low = a ^ b;  // XOR_Gate xor_1, 32 bits wide
endmodule

module or_circuit (
  input  [31:0] a,
  input  [31:0] b,
  output [31:0] res_low
);

  assign res_low = a | b;  // OR_Gate or_1, 32 bits wide
endmodule

module and_circuit (
  input  [31:0] a,
  input  [31:0] b,
  output [31:0] res_low
);

  assign res_low = a & b;  // AND_Gate and_1, 32 bits wide
endmodule

module add_circuit (
  input  c_in,
  input  [31:0] a,
  input  [31:0] b,
  output [63:0] res
);

  wire adder_1_cout, adder_2_cout, adder_3_cout, adder_4_cout, adder_5_cout, adder_6_cout, adder_7_cout,
       adder_8_cout, adder_9_cout, adder_10_cout, adder_11_cout, adder_12_cout, adder_13_cout, adder_14_cout,
       adder_15_cout, multiplexer_1_out, multiplexer_2_out, multiplexer_3_out, multiplexer_4_out,
       multiplexer_5_out, multiplexer_6_out;
  wire [3:0] adder_1_out, adder_2_out, adder_3_out, adder_4_out, adder_5_out, adder_6_out, adder_7_out,
       adder_9_out, adder_10_out, adder_11_out, adder_12_out, adder_13_out, adder_14_out, adder_15_out;

  Adder #(.width(4)) adder_1 (.a(a[7:4]), .b(b[7:4]), .out(adder_1_out), .cout(adder_1_cout));  // open: cin
  Adder #(.width(4)) adder_2 (.a(a[11:8]), .b(b[11:8]), .out(adder_2_out), .cout(adder_2_cout));  // open: cin
  Adder #(.width(4)) adder_3 (.a(a[15:12]), .b(b[15:12]), .out(adder_3_out), .cout(adder_3_cout));  // open: cin
  Adder #(.width(4)) adder_4 (.a(a[19:16]), .b(b[19:16]), .out(adder_4_out), .cout(adder_4_cout));  // open: cin
  Adder #(.width(4)) adder_5 (.a(a[23:20]), .b(b[23:20]), .out(adder_5_out), .cout(adder_5_cout));  // open: cin
  Adder #(.width(4)) adder_6 (.a(a[27:24]), .b(b[27:24]), .out(adder_6_out), .cout(adder_6_cout));  // open: cin
  Adder #(.width(4)) adder_7 (.a(a[31:28]), .b(b[31:28]), .out(adder_7_out), .cout(adder_7_cout));  // open: cin
  Adder #(.width(4)) adder_8 (.a(a[3:0]), .b(b[3:0]), .out(res[3:0]), .cin(c_in), .cout(adder_8_cout));
  Adder #(.width(4)) adder_9 (.a(a[7:4]), .b(b[7:4]), .out(adder_9_out), .cin(1'b1), .cout(adder_9_cout));
  Adder #(.width(4)) adder_10 (.a(a[11:8]), .b(b[11:8]), .out(adder_10_out), .cin(1'b1), .cout(adder_10_cout));
  Adder #(.width(4)) adder_11 (.a(a[15:12]), .b(b[15:12]), .out(adder_11_out), .cin(1'b1), .cout(adder_11_cout));
  Adder #(.width(4)) adder_12 (.a(a[19:16]), .b(b[19:16]), .out(adder_12_out), .cin(1'b1), .cout(adder_12_cout));
  Adder #(.width(4)) adder_13 (.a(a[23:20]), .b(b[23:20]), .out(adder_13_out), .cin(1'b1), .cout(adder_13_cout));
  Adder #(.width(4)) adder_14 (.a(a[27:24]), .b(b[27:24]), .out(adder_14_out), .cin(1'b1), .cout(adder_14_cout));
  Adder #(.width(4)) adder_15 (.a(a[31:28]), .b(b[31:28]), .out(adder_15_out), .cin(1'b1), .cout(adder_15_cout));
  Multiplexer multiplexer_1 (.in0(adder_1_cout), .in1(adder_9_cout), .out(multiplexer_1_out), .sel(adder_8_cout));
  Multiplexer multiplexer_2 (.in0(adder_2_cout), .in1(adder_10_cout), .out(multiplexer_2_out), .sel(multiplexer_1_out));
  Multiplexer multiplexer_3 (.in0(adder_3_cout), .in1(adder_11_cout), .out(multiplexer_3_out), .sel(multiplexer_2_out));
  Multiplexer multiplexer_4 (.in0(adder_4_cout), .in1(adder_12_cout), .out(multiplexer_4_out), .sel(multiplexer_3_out));
  Multiplexer multiplexer_5 (.in0(adder_5_cout), .in1(adder_13_cout), .out(multiplexer_5_out), .sel(multiplexer_4_out));
  Multiplexer multiplexer_6 (.in0(adder_6_cout), .in1(adder_14_cout), .out(multiplexer_6_out), .sel(multiplexer_5_out));
  Multiplexer multiplexer_7 (.in0(adder_7_cout), .in1(adder_15_cout), .out(res[32]), .sel(multiplexer_6_out));
  Multiplexer #(.width(4)) multiplexer_8 (.in0(adder_1_out), .in1(adder_9_out), .out(res[7:4]), .sel(adder_8_cout));
  Multiplexer #(.width(4)) multiplexer_9 (
    .in0(adder_2_out), .in1(adder_10_out), .out(res[11:8]), .sel(multiplexer_1_out));
  Multiplexer #(.width(4)) multiplexer_10 (
    .in0(adder_3_out), .in1(adder_11_out), .out(res[15:12]), .sel(multiplexer_2_out));
  Multiplexer #(.width(4)) multiplexer_11 (
    .in0(adder_4_out), .in1(adder_12_out), .out(res[19:16]), .sel(multiplexer_3_out));
  Multiplexer #(.width(4)) multiplexer_12 (
    .in0(adder_5_out), .in1(adder_13_out), .out(res[23:20]), .sel(multiplexer_4_out));
  Multiplexer #(.width(4)) multiplexer_13 (
    .in0(adder_6_out), .in1(adder_14_out), .out(res[27:24]), .sel(multiplexer_5_out));
  Multiplexer #(.width(4)) multiplexer_14 (
    .in0(adder_7_out), .in1(adder_15_out), .out(res[31:28]), .sel(multiplexer_6_out));

  assign res[63:33] = {31{1'b0}};
endmodule

module sub_circuit (
  input  [31:0] a,
  input  [31:0] b,
  output [63:0] res
);

  wire [63:0] bit_extender_1_out, bit_extender_2_out;

  assign bit_extender_1_out = {{32{1'b0}}, a};  // Bit_Extender bit_extender_1
  assign bit_extender_2_out = {{32{1'b0}}, b};  // Bit_Extender bit_extender_2
  Subtractor #(.width(64)) subtractor_1 (.a(bit_extender_1_out), .b(bit_extender_2_out), .out(res));  // open: bin, bout
endmodule

module div_circuit (
  input  [31:0] divisor,
  input  [31:0] dividend,
  input  start,
  input  clk,
  output [31:0] quotient,
  output [31:0] remainder,
  output done
);

  wire and_1_out, bitselector_1_out, comparator_1_eq, comparator_2_lt, not_1_out, not_2_out;
  wire [6:0] counter_q, multiplexer_4_out, multiplexer_8_out, subtractor_1_out;
  wire [31:0] A_q, adder_1_out, B_q, bit_extender_1_out, multiplexer_1_out, multiplexer_2_out,
       multiplexer_3_out, multiplexer_5_out, multiplexer_6_out, multiplexer_7_out, multiplexer_9_out,
       multiplexer_10_out, or_1_out, Q_q, shifter_1_out, shifter_2_out, subtractor_2_out;

  Multiplexer #(.width(32)) multiplexer_1 (
    .in0(multiplexer_9_out), .in1({32{1'b0}}), .out(multiplexer_1_out), .sel(start));
  Multiplexer #(.width(32)) multiplexer_2 (.in0(B_q), .in1(divisor), .out(multiplexer_2_out), .sel(start));
  Multiplexer #(.width(32)) multiplexer_3 (
    .in0(multiplexer_10_out), .in1(dividend), .out(multiplexer_3_out), .sel(start));
  Multiplexer #(.width(7)) multiplexer_4 (
    .in0(multiplexer_8_out), .in1(7'b0100000), .out(multiplexer_4_out), .sel(start));
  Subtractor #(.width(7)) subtractor_1 (.a(counter_q), .b(7'b0000001), .out(subtractor_1_out));  // open: bin, bout
  Multiplexer #(.width(32)) multiplexer_5 (.in0(multiplexer_1_out), .in1(A_q), .out(multiplexer_5_out), .sel(done));
  Multiplexer #(.width(32)) multiplexer_6 (.in0(multiplexer_2_out), .in1(B_q), .out(multiplexer_6_out), .sel(done));
  Multiplexer #(.width(32)) multiplexer_7 (.in0(multiplexer_3_out), .in1(Q_q), .out(multiplexer_7_out), .sel(done));
  Register #(.width(32)) A (.D(multiplexer_5_out), .en(1'b1), .clk(clk), .Q(A_q));  // open: clr
  Register #(.width(32)) B (.D(multiplexer_6_out), .en(1'b1), .clk(clk), .Q(B_q));  // open: clr
  Register #(.width(32)) Q (.D(multiplexer_7_out), .en(1'b1), .clk(clk), .Q(Q_q));  // open: clr
  Register #(.width(7)) counter (.D(multiplexer_4_out), .en(1'b1), .clk(clk), .Q(counter_q));  // open: clr
  Shifter #(.width(32)) shifter_1 (.in(A_q), .\dist (5'b00001), .out(shifter_1_out));
  BitSelector #(.width(32)) bitselector_1 (.in(Q_q), .out(bitselector_1_out), .sel({5{1'b1}}));
  Comparator #(.mode("unsigned"), .width(7)) comparator_1 (
    .a(counter_q), .b({7{1'b0}}), .eq(comparator_1_eq));  // open: gt, lt
  assign bit_extender_1_out = {{31{1'b0}}, bitselector_1_out};  // Bit_Extender bit_extender_1
  Adder #(.width(32)) adder_1 (.a(shifter_1_out), .b(bit_extender_1_out), .out(adder_1_out));  // open: cin, cout
  Shifter #(.width(32)) shifter_2 (.in(Q_q), .\dist (5'b00001), .out(shifter_2_out));
  Multiplexer #(.width(7)) multiplexer_8 (
    .in0(subtractor_1_out), .in1(counter_q), .out(multiplexer_8_out), .sel(comparator_1_eq));
  Subtractor #(.width(32)) subtractor_2 (.a(adder_1_out), .b(B_q), .out(subtractor_2_out));  // open: bin, bout
  Comparator #(.mode("unsigned"), .width(32)) comparator_2 (
    .a(adder_1_out), .b(B_q), .lt(comparator_2_lt));  // open: gt, eq
  not not_1 (not_1_out, comparator_2_lt);
  assign or_1_out = shifter_2_out | 32'h1;  // OR_Gate or_1, 32 bits wide
  and and_1 (and_1_out, comparator_1_eq, not_2_out);
  not not_2 (not_2_out, start);
  Multiplexer #(.width(32)) multiplexer_9 (
    .in0(adder_1_out), .in1(subtractor_2_out), .out(multiplexer_9_out), .sel(not_1_out));
  Multiplexer #(.width(32)) multiplexer_10 (
    .in0(shifter_2_out), .in1(or_1_out), .out(multiplexer_10_out), .sel(not_1_out));
  Multiplexer #(.width(32)) multiplexer_11 (.in1(Q_q), .out(quotient), .sel(and_1_out));  // open: in0
  Multiplexer #(.width(32)) multiplexer_12 (.in1(A_q), .out(remainder), .sel(and_1_out));  // open: in0
  Multiplexer multiplexer_13 (.in0(1'b0), .in1(1'b1), .out(done), .sel(and_1_out));

  // Notes on the sheet:
  //   divisor: initial=0xc4018d88
  //   dividend: initial=0x82fbf905
  //   clk: initial=0x1
endmodule

module clo_circuit (
  input  [31:0] A,
  output [5:0] res
);

  wire [31:0] not_1_out;

  assign not_1_out = ~A;  // NOT_Gate not_1, 32 bits wide
  clz_circuit clz_circuit_1 (.A(not_1_out), .out_2(res));
endmodule

module clz_circuit (
  input  [31:0] A,
  output [5:0] out_2
);

  wire comparator_2_eq;
  wire [1:0] multiplexer_5_out;
  wire [3:0] multiplexer_4_out;
  wire [4:0] not_1_out;
  wire [7:0] multiplexer_3_out;
  wire [15:0] multiplexer_1_out;

  Comparator #(.mode("unsigned"), .width(16)) comparator_1 (
    .a(A[31:16]), .b({16{1'b0}}), .eq(not_1_out[4]));  // open: gt, lt
  Comparator #(.mode("unsigned"), .width(32)) comparator_2 (
    .a(A), .b({32{1'b0}}), .eq(comparator_2_eq));  // open: gt, lt
  Multiplexer #(.width(16)) multiplexer_1 (.in0(A[31:16]), .in1(A[15:0]), .out(multiplexer_1_out), .sel(not_1_out[4]));
  Multiplexer #(.width(6)) multiplexer_2 (.in0({1'b0, not_1_out}), .in1(6'b100000), .out(out_2), .sel(comparator_2_eq));
  Comparator #(.mode("unsigned")) comparator_3 (
    .a(multiplexer_1_out[15:8]), .b({8{1'b0}}), .eq(not_1_out[3]));  // open: gt, lt
  Multiplexer #(.width(8)) multiplexer_3 (
    .in0(multiplexer_1_out[15:8]), .in1(multiplexer_1_out[7:0]), .out(multiplexer_3_out), .sel(not_1_out[3]));
  Comparator #(.mode("unsigned"), .width(4)) comparator_4 (
    .a(multiplexer_3_out[7:4]), .b(4'b0000), .eq(not_1_out[2]));  // open: gt, lt
  Multiplexer #(.width(4)) multiplexer_4 (
    .in0(multiplexer_3_out[7:4]), .in1(multiplexer_3_out[3:0]), .out(multiplexer_4_out), .sel(not_1_out[2]));
  Multiplexer #(.width(2)) multiplexer_5 (
    .in0(multiplexer_4_out[3:2]), .in1(multiplexer_4_out[1:0]), .out(multiplexer_5_out), .sel(not_1_out[1]));
  Comparator #(.mode("unsigned"), .width(2)) comparator_5 (
    .a(multiplexer_4_out[3:2]), .b(2'b00), .eq(not_1_out[1]));  // open: gt, lt
  not not_1 (not_1_out[0], multiplexer_5_out[1]);
endmodule

module sll_circuit (
  input  [31:0] a,
  input  [4:0] num_shift,
  output [63:0] result
);

  wire [1:0] multiplexer_1_out;
  wire [7:0] multiplexer_3_out;
  wire [15:0] multiplexer_4_out;
  wire [63:0] extended;
  wire [63:2] s2;
  wire [63:4] s3;
  wire [63:8] s4;
  wire [63:16] s5;
  wire [63:60] multiplexer_2_out;

  assign extended = {{32{1'b0}}, a};  // Bit_Extender bit_extender_1
  Multiplexer #(.width(64)) multiplexer_1 (
    .in0(extended), .in1({extended[62:0], 1'b0}), .out({multiplexer_1_out, s2}), .sel(num_shift[0]));
  Multiplexer #(.width(64)) multiplexer_2 (
    .in0({multiplexer_1_out, s2}), .in1({s2, 2'b00}), .out({multiplexer_2_out, s3}), .sel(num_shift[1]));
  Multiplexer #(.width(64)) multiplexer_3 (
    .in0({multiplexer_2_out, s3}), .in1({s3, 4'b0000}), .out({multiplexer_3_out, s4}), .sel(num_shift[2]));
  Multiplexer #(.width(64)) multiplexer_4 (
    .in0({multiplexer_3_out, s4}), .in1({s4, {8{1'b0}}}), .out({multiplexer_4_out, s5}), .sel(num_shift[3]));
  Multiplexer #(.width(64)) multiplexer_5 (
    .in0({multiplexer_4_out, s5}), .in1({s5, {16{1'b0}}}), .out(result), .sel(num_shift[4]));

  // Other names for the same wires on the sheet: s1[63:1] = extended[62:0]; bit0 = num_shift[0]; bit1 = num_shift[1];
  //   bit2 = num_shift[2]; bit3 = num_shift[3]; bit4 = num_shift[4]
endmodule

module srl_circuit (
  input  [31:0] a,
  input  [4:0] num_shift,
  output [63:0] result
);

  wire [1:0] multiplexer_1_out;
  wire [3:0] multiplexer_2_out;
  wire [7:0] multiplexer_3_out;
  wire [15:0] multiplexer_4_out;
  wire [47:0] s5;
  wire [55:0] s4;
  wire [59:0] s3;
  wire [61:0] s2;
  wire [63:0] extended;

  assign extended = {{32{1'b0}}, a};  // Bit_Extender bit_extender_1
  Multiplexer #(.width(64)) multiplexer_1 (
    .in0(extended), .in1({1'b0, extended[63:1]}), .out({s2, multiplexer_1_out}), .sel(num_shift[0]));
  Multiplexer #(.width(64)) multiplexer_2 (
    .in0({s2, multiplexer_1_out}), .in1({2'b00, s2}), .out({s3, multiplexer_2_out}), .sel(num_shift[1]));
  Multiplexer #(.width(64)) multiplexer_3 (
    .in0({s3, multiplexer_2_out}), .in1({4'b0000, s3}), .out({s4, multiplexer_3_out}), .sel(num_shift[2]));
  Multiplexer #(.width(64)) multiplexer_4 (
    .in0({s4, multiplexer_3_out}), .in1({{8{1'b0}}, s4}), .out({s5, multiplexer_4_out}), .sel(num_shift[3]));
  Multiplexer #(.width(64)) multiplexer_5 (
    .in0({s5, multiplexer_4_out}), .in1({{16{1'b0}}, s5}), .out(result), .sel(num_shift[4]));

  // Other names for the same wires on the sheet: bit0 = num_shift[0]; bit1 = num_shift[1]; bit2 = num_shift[2];
  //   bit3 = num_shift[3]; bit4 = num_shift[4]; s1[62:0] = extended[63:1]
endmodule

module sra_circuit (
  input  [31:0] a,
  input  [4:0] num_shift,
  output [63:0] result
);

  wire [63:0] extended, multiplexer_1_out, multiplexer_2_out, multiplexer_3_out, multiplexer_4_out, s2, s3,
       s4, s5;

  assign extended = {{32{1'b0}}, a};  // Bit_Extender bit_extender_1
  Multiplexer #(.width(64)) multiplexer_1 (
    .in0(extended), .in1({{2{extended[63]}}, extended[62:1]}), .out(multiplexer_1_out), .sel(num_shift[0]));
  Multiplexer #(.width(64)) multiplexer_2 (
    .in0(multiplexer_1_out), .in1({s2[63:62], s2[63:62], s2[59:0]}), .out(multiplexer_2_out),
    .sel(num_shift[1]));
  Multiplexer #(.width(64)) multiplexer_3 (
    .in0(multiplexer_2_out), .in1({s3[63:60], s3[63:60], s3[55:0]}), .out(multiplexer_3_out),
    .sel(num_shift[2]));
  Multiplexer #(.width(64)) multiplexer_4 (
    .in0(multiplexer_3_out), .in1({s4[63:56], s4[63:56], s4[47:0]}), .out(multiplexer_4_out),
    .sel(num_shift[3]));
  Multiplexer #(.width(64)) multiplexer_5 (
    .in0(multiplexer_4_out), .in1({s5[63:48], s5[63:48], s5[31:0]}), .out(result), .sel(num_shift[4]));

  // Other names for the same wires on the sheet: bit0 = num_shift[0]; bit1 = num_shift[1]; bit2 = num_shift[2];
  //   bit3 = num_shift[3]; bit4 = num_shift[4]; s1[63:0] = {{2{extended[63]}}, extended[62:1]};
  //   stage_1[63:2] = {s2[63:62], s2[59:0]}; s2[61:60] = s2[63:62]; stage_2[63:4] = {s3[63:60], s3[55:0]};
  //   s3[59:56] = s3[63:60]; stage_3[63:8] = {s4[63:56], s4[47:0]}; s4[55:48] = s4[63:56];
  //   stage_4[63:16] = {s5[63:48], s5[31:0]}; s5[47:32] = s5[63:48]
endmodule

module rotr_circuit (
  input  [31:0] a,
  input  [4:0] num_shift,
  output [31:0] result
);

  wire [31:0] multiplexer_1_out, multiplexer_2_out, multiplexer_3_out, multiplexer_4_out, s1, s2, s3, s4, s5;

  Multiplexer #(.width(32)) multiplexer_1 (.in0(a), .in1(s1), .out(multiplexer_1_out), .sel(num_shift[0]));
  Multiplexer #(.width(32)) multiplexer_2 (
    .in0(multiplexer_1_out), .in1(s2), .out(multiplexer_2_out), .sel(num_shift[1]));
  Multiplexer #(.width(32)) multiplexer_3 (
    .in0(multiplexer_2_out), .in1(s3), .out(multiplexer_3_out), .sel(num_shift[2]));
  Multiplexer #(.width(32)) multiplexer_4 (
    .in0(multiplexer_3_out), .in1(s4), .out(multiplexer_4_out), .sel(num_shift[3]));
  Multiplexer #(.width(32)) multiplexer_5 (.in0(multiplexer_4_out), .in1(s5), .out(result), .sel(num_shift[4]));

  // Other names for the same wires on the sheet: extended[31:0] = a; bit0 = num_shift[0]; bit1 = num_shift[1];
  //   bit2 = num_shift[2]; bit3 = num_shift[3]; bit4 = num_shift[4]; stage_1[31:0] = {s2[29:0], s2[31:30]};
  //   stage_2[31:0] = {s3[27:0], s3[31:28]}; stage_3[31:0] = {s4[23:0], s4[31:24]};
  //   stage_4[31:0] = {s5[15:0], s5[31:16]}
endmodule

module Carry_Select_Adder (
  input  c_in,
  input  [31:0] a,
  input  [31:0] b,
  output [63:0] res
);

  wire adder_1_cout, adder_2_cout, adder_3_cout, adder_4_cout, adder_5_cout, adder_6_cout, adder_7_cout,
       adder_8_cout, adder_9_cout, adder_10_cout, adder_11_cout, adder_12_cout, adder_13_cout, adder_14_cout,
       adder_15_cout, multiplexer_1_out, multiplexer_2_out, multiplexer_3_out, multiplexer_4_out,
       multiplexer_5_out, multiplexer_6_out;
  wire [3:0] adder_1_out, adder_2_out, adder_3_out, adder_4_out, adder_5_out, adder_6_out, adder_7_out,
       adder_9_out, adder_10_out, adder_11_out, adder_12_out, adder_13_out, adder_14_out, adder_15_out;

  Adder #(.width(4)) adder_1 (.a(a[7:4]), .b(b[7:4]), .out(adder_1_out), .cout(adder_1_cout));  // open: cin
  Adder #(.width(4)) adder_2 (.a(a[11:8]), .b(b[11:8]), .out(adder_2_out), .cout(adder_2_cout));  // open: cin
  Adder #(.width(4)) adder_3 (.a(a[15:12]), .b(b[15:12]), .out(adder_3_out), .cout(adder_3_cout));  // open: cin
  Adder #(.width(4)) adder_4 (.a(a[19:16]), .b(b[19:16]), .out(adder_4_out), .cout(adder_4_cout));  // open: cin
  Adder #(.width(4)) adder_5 (.a(a[23:20]), .b(b[23:20]), .out(adder_5_out), .cout(adder_5_cout));  // open: cin
  Adder #(.width(4)) adder_6 (.a(a[27:24]), .b(b[27:24]), .out(adder_6_out), .cout(adder_6_cout));  // open: cin
  Adder #(.width(4)) adder_7 (.a(a[31:28]), .b(b[31:28]), .out(adder_7_out), .cout(adder_7_cout));  // open: cin
  Adder #(.width(4)) adder_8 (.a(a[3:0]), .b(b[3:0]), .out(res[3:0]), .cin(c_in), .cout(adder_8_cout));
  Adder #(.width(4)) adder_9 (.a(a[7:4]), .b(b[7:4]), .out(adder_9_out), .cin(1'b1), .cout(adder_9_cout));
  Adder #(.width(4)) adder_10 (.a(a[11:8]), .b(b[11:8]), .out(adder_10_out), .cin(1'b1), .cout(adder_10_cout));
  Adder #(.width(4)) adder_11 (.a(a[15:12]), .b(b[15:12]), .out(adder_11_out), .cin(1'b1), .cout(adder_11_cout));
  Adder #(.width(4)) adder_12 (.a(a[19:16]), .b(b[19:16]), .out(adder_12_out), .cin(1'b1), .cout(adder_12_cout));
  Adder #(.width(4)) adder_13 (.a(a[23:20]), .b(b[23:20]), .out(adder_13_out), .cin(1'b1), .cout(adder_13_cout));
  Adder #(.width(4)) adder_14 (.a(a[27:24]), .b(b[27:24]), .out(adder_14_out), .cin(1'b1), .cout(adder_14_cout));
  Adder #(.width(4)) adder_15 (.a(a[31:28]), .b(b[31:28]), .out(adder_15_out), .cin(1'b1), .cout(adder_15_cout));
  Multiplexer multiplexer_1 (.in0(adder_1_cout), .in1(adder_9_cout), .out(multiplexer_1_out), .sel(adder_8_cout));
  Multiplexer multiplexer_2 (.in0(adder_2_cout), .in1(adder_10_cout), .out(multiplexer_2_out), .sel(multiplexer_1_out));
  Multiplexer multiplexer_3 (.in0(adder_3_cout), .in1(adder_11_cout), .out(multiplexer_3_out), .sel(multiplexer_2_out));
  Multiplexer multiplexer_4 (.in0(adder_4_cout), .in1(adder_12_cout), .out(multiplexer_4_out), .sel(multiplexer_3_out));
  Multiplexer multiplexer_5 (.in0(adder_5_cout), .in1(adder_13_cout), .out(multiplexer_5_out), .sel(multiplexer_4_out));
  Multiplexer multiplexer_6 (.in0(adder_6_cout), .in1(adder_14_cout), .out(multiplexer_6_out), .sel(multiplexer_5_out));
  Multiplexer multiplexer_7 (.in0(adder_7_cout), .in1(adder_15_cout), .out(res[32]), .sel(multiplexer_6_out));
  Multiplexer #(.width(4)) multiplexer_8 (.in0(adder_1_out), .in1(adder_9_out), .out(res[7:4]), .sel(adder_8_cout));
  Multiplexer #(.width(4)) multiplexer_9 (
    .in0(adder_2_out), .in1(adder_10_out), .out(res[11:8]), .sel(multiplexer_1_out));
  Multiplexer #(.width(4)) multiplexer_10 (
    .in0(adder_3_out), .in1(adder_11_out), .out(res[15:12]), .sel(multiplexer_2_out));
  Multiplexer #(.width(4)) multiplexer_11 (
    .in0(adder_4_out), .in1(adder_12_out), .out(res[19:16]), .sel(multiplexer_3_out));
  Multiplexer #(.width(4)) multiplexer_12 (
    .in0(adder_5_out), .in1(adder_13_out), .out(res[23:20]), .sel(multiplexer_4_out));
  Multiplexer #(.width(4)) multiplexer_13 (
    .in0(adder_6_out), .in1(adder_14_out), .out(res[27:24]), .sel(multiplexer_5_out));
  Multiplexer #(.width(4)) multiplexer_14 (
    .in0(adder_7_out), .in1(adder_15_out), .out(res[31:28]), .sel(multiplexer_6_out));

  assign res[63:33] = {31{1'b0}};
endmodule

module Shift_Logical_Left_circuit (
  input  [4:0] shamt,
  input  [31:0] A,
  output [63:0] res
);

  wire [63:2] shift_2;
  wire [63:4] shift_4;
  wire [63:7] shift_8;
  wire [63:16] shift_16;
  wire [63:48] stage_8;
  wire [63:57] stage_4;
  wire [63:60] stage_2;
  wire [63:62] stage_1;

  Multiplexer #(.width(64)) multiplexer_1 (
    .in0({stage_8, shift_16}), .in1({shift_16, {16{1'b0}}}), .out(res), .sel(shamt[4]));
  Multiplexer #(.width(64)) multiplexer_2 (
    .in0({stage_1, shift_2}), .in1({shift_2, 2'b00}), .out({stage_2, shift_4}), .sel(shamt[1]));
  Multiplexer #(.width(64)) multiplexer_3 (
    .in0({stage_2, shift_4}), .in1({shift_4, 4'b0000}), .out({stage_4, shift_8}), .sel(shamt[2]));
  Multiplexer #(.width(64)) multiplexer_4 (
    .in0({{32{1'b0}}, A}), .in1({{31{1'b0}}, A, 1'b0}), .out({stage_1, shift_2}), .sel(shamt[0]));
  Multiplexer #(.width(64)) multiplexer_5 (
    .in0({stage_4, shift_8}), .in1({shift_8, {7{1'b0}}}), .out({stage_8, shift_16}), .sel(shamt[3]));

  // Other names for the same wires on the sheet: b0 = shamt[0]; b1 = shamt[1]; b2 = shamt[2]; b3 = shamt[3];
  //   b4 = shamt[4]; extended_64[31:0] = A; shift_1[32:1] = A; stage_2[59:0] = shift_4; stage_8[47:0] = shift_16;
  //   stage_1[61:0] = shift_2; stage_4[56:0] = shift_8; stage_16[63:0] = res
endmodule

module CSA (
  input  [31:0] a,
  input  [31:0] b,
  input  [31:0] c,
  input  c_in,
  output [63:0] res
);

  wire [31:0] and_1_out, and_2_out, and_3_out, carry_out, sum_out;
  wire [63:0] shift_logical_left_circuit_1_res;

  assign sum_out = a ^ b ^ c;  // XOR_Gate sum, 32 bits wide
  assign and_1_out = a & b;  // AND_Gate and_1, 32 bits wide
  assign and_2_out = b & c;  // AND_Gate and_2, 32 bits wide
  assign carry_out = and_1_out | and_2_out | and_3_out;  // OR_Gate carry, 32 bits wide
  assign and_3_out = a & c;  // AND_Gate and_3, 32 bits wide
  Shift_Logical_Left_circuit shift_logical_left_circuit_1 (
    .shamt(5'b00001), .A(carry_out), .res(shift_logical_left_circuit_1_res));
  Carry_Select_Adder carry_select_adder_1 (
    .c_in(c_in), .a(sum_out), .b(shift_logical_left_circuit_1_res[31:0]), .res(res));
endmodule

module multiplier_circuit (
  input  [31:0] a,
  input  in_2,
  input  [31:0] B,
  output done,
  output [63:0] ans
);

  wire clk, comparator_1_lt, not_1_out;
  wire [5:0] adder_1_out, counter, multiplexer_5_out, multiplexer_6_out;
  wire [31:0] a_t, b_t, csa_1_p4, multiplexer_4_out, x, y, z;
  wire [63:0] adder_2_out, bit_extender_1_out, multiplexer_7_out, sll_circuit_1_result, srl_circuit_1_result;

  Clock clock_1 (.out(clk));
  assign bit_extender_1_out = {{32{a_t[31]}}, a_t};  // Bit_Extender bit_extender_1
  Multiplexer #(.select(2), .width(32)) multiplexer_1 (
    .in0({32{1'b0}}), .in1(b_t), .in2(b_t), .in3(b_t), .out(x), .sel(a_t[1:0]));
  Multiplexer #(.select(2), .width(32)) multiplexer_2 (
    .in0({32{1'b0}}), .in1({32{1'b0}}), .in2(b_t), .in3(b_t), .out(y), .sel(a_t[1:0]));
  Multiplexer #(.select(2), .width(32)) multiplexer_3 (
    .in0({32{1'b0}}), .in1({32{1'b0}}), .in2({32{1'b0}}), .in3(b_t), .out(z), .sel(a_t[1:0]));
  srl_circuit srl_circuit_1 (.a(bit_extender_1_out[31:0]), .num_shift(5'b00010), .result(srl_circuit_1_result));
  Register #(.width(32)) register_1 (.D(B), .en(in_2), .clk(clk), .Q(b_t));  // open: clr
  Multiplexer #(.width(32)) multiplexer_4 (
    .in0(srl_circuit_1_result[31:0]), .in1(a), .out(multiplexer_4_out), .sel(in_2));
  Register #(.width(32)) register_2 (.D(multiplexer_4_out), .en(1'b1), .clk(clk), .Q(a_t));  // open: clr
  Adder #(.width(6)) adder_1 (.a(counter), .b(6'b000010), .out(adder_1_out));  // open: cin, cout
  Comparator #(.width(6)) comparator_1 (.a(counter), .b(6'b110010), .lt(comparator_1_lt));  // open: gt, eq
  Multiplexer #(.width(6)) multiplexer_5 (.in0(counter), .in1({6{1'b0}}), .out(multiplexer_5_out), .sel(not_1_out));
  not not_1 (not_1_out, comparator_1_lt);
  Multiplexer #(.width(6)) multiplexer_6 (.in0(adder_1_out), .in1({6{1'b0}}), .out(multiplexer_6_out), .sel(in_2));
  Register #(.width(6)) register_3 (.D(multiplexer_6_out), .en(1'b1), .clk(clk), .Q(counter));  // open: clr
  // CSA csa_1: pin names not known; wires that end beside it: x, y, z, csa_1_p4
  Comparator #(.width(32)) comparator_2 (.a(a_t), .b({32{1'b0}}), .eq(done));  // open: gt, lt
  sll_circuit sll_circuit_1 (.a(csa_1_p4), .num_shift(multiplexer_5_out[4:0]), .result(sll_circuit_1_result));
  Adder #(.width(64)) adder_2 (.a(ans), .b(sll_circuit_1_result), .out(adder_2_out), .cin(1'b0));  // open: cout
  Multiplexer #(.width(64)) multiplexer_7 (.in0(adder_2_out), .in1({64{1'b0}}), .out(multiplexer_7_out), .sel(in_2));
  Register #(.width(64)) register_4 (.D(multiplexer_7_out), .en(1'b1), .clk(clk), .Q(ans));  // open: clr
  // Pins of 32 and 64 bits meet at bit_extender_1_out

  // Other names for the same wires on the sheet: start = in_2
endmodule

module add_circ (
  input  [31:0] a,
  input  [31:0] b,
  output [31:0] res_low,
  output [31:0] res_high
);

  wire adder_1_cout;

  Adder #(.width(32)) adder_1 (.a(a), .b(b), .out(res_low), .cin(1'b0), .cout(adder_1_cout));
  assign res_high = {{31{1'b0}}, adder_1_cout};  // Bit_Extender bit_extender_1
endmodule
